# Fritzing sketch comedouro (saved by Fritzing 0.9.3b)

parts:
  Part1 = Arduino Uno (Rev3) - ICSP
  hc-sr1 = hc-sr04

nets:
  N1: Part1.D2, hc-sr1.Echo
  N2: Part1.D3_PWM, hc-sr1.Trig

notes:
  Stepper
  1n1
  1n2
  1n3
  1n4
  5v
  gnd
  RFID
  SS pin
  sck
  mosi
  miso
  rst
  gnd
