# Fritzing sketch esp8266 (saved by Fritzing 0.9.3b)

parts:
  U2 = ESP8266 WiFi Module [part_number=ESP8266]
  Componente1 = Arduino Uno (Rev3)
  VCC1 = Battery

nets:
  GND: U2.RST, U2.GND, Componente1.GND, VCC1.-
  3.3V: U2.CHIP_EN, U2.3.3V, Componente1.3V3, VCC1.+
  N1: U2.TX, Componente1.D1/TX
  N2: U2.RX, Componente1.D0/RX
